# Fritzing sketch Setup (saved by Fritzing 0.9.3b)
breadboards: 1

parts:
  Raspberry_Pi_1 = Raspberry Pi 3 [part_number=RPI-3-V1.2]
  LED1 = RGB LED - (4 legs) [package="5 mm [THT]"]
  LED2 = RGB LED - (4 legs) [package="5 mm [THT]"]
  R1 = Resistor [tolerance=±5% resistance=1k package="0805 [SMD]"]
  R2 = Resistor [tolerance=±5% resistance=1k package="0805 [SMD]"]
  R3 = Resistor [tolerance=±5% resistance=1k package="0805 [SMD]"]
  R4 = Resistor [tolerance=±5% resistance=1k package="0805 [SMD]"]
  R5 = Resistor [tolerance=±5% resistance=1k package="0805 [SMD]"]
  R6 = Resistor [tolerance=±5% resistance=1k package="0805 [SMD]"]
  LED4 = smd LED [color="Red (633nm)" package="1206 [SMD]"]
  R7 = Resistor [tolerance=±5% resistance=100 package="0805 [SMD]"]
  LED5 = smd LED [color="Yellow (595nm)" package="1206 [SMD]"]
  LED6 = smd LED [color="Green (555nm)" package="1206 [SMD]"]
  R8 = Resistor [tolerance=±5% resistance=100 package="0805 [SMD]"]
  R9 = Resistor [tolerance=±5% resistance=100 package="0805 [SMD]"]

nets:
  N1: Raspberry_Pi_1.GIPO4, R9.Pin_0
  N2: Raspberry_Pi_1.GIPO17, R8.Pin_0
  N3: Raspberry_Pi_1.GIPO27, R7.Pin_0
  N4: Raspberry_Pi_1.GND, LED1.common_anode, LED2.common_anode, LED4.cathode, LED5.cathode, LED6.cathode
  N5: Raspberry_Pi_1.GIPO21, R3.Pin_1, R4.Pin_1
  N6: Raspberry_Pi_1.GIPO20, R2.Pin_1, R6.Pin_1
  N7: Raspberry_Pi_1.GIPO16, R1.Pin_1, R5.Pin_1
  N8: LED1.red_cathode, R1.Pin_0
  N9: LED1.green_cathode, R2.Pin_0
  N10: LED1.blue_cathode, R3.Pin_0
  N11: LED2.red_cathode, R5.Pin_0
  N12: LED2.green_cathode, R6.Pin_0
  N13: LED2.blue_cathode, R4.Pin_0
  N14: LED4.anode, R9.Pin_1
  N15: R7.Pin_1, LED6.anode
  N16: LED5.anode, R8.Pin_1
